# Fritzing sketch final Design (saved by Fritzing 0.9.3b)
circuit board: 5.6cm x 6.6cm
breadboards: 1

parts:
  Device_Output = Audio Jack (TRS) 3.5mm [package="PG203J [THT]"]
  DC_12V_JACK = Power plug
  Blue_LED = LED - 5mm [color="Red (633nm)" package="5 mm [THT]"]
  Green_LED = LED - 5mm [color="Red (633nm)" package="5 mm [THT]"]
  5V_volt = Voltage Regulator - 5V [package="TO220 [THT]"]
  Red_LED = LED - 5mm [color="Red (633nm)" package="5 mm [THT]"]
  R1 = Resistor [tolerance=±5% resistance=220 package=THT]
  Buzzer = Buzzer 12mm [package=buzzer-12mm-ns-kit]
  R2 = Resistor [tolerance=±5% resistance=220 package=THT]
  ATMEGA_328P = atmega328 [package=dip]
  10K = Resistor [tolerance=±5% resistance=220 package=THT]
  Reset = Pushbutton [package="[THT]"]
  10UF = Electrolytic Capacitor [capacitance=1µF package="100 mil [THT, electrolytic]"]
  16MHz_C = Crystal [frequency="16 Mhz" package=THT]
  22pf = Ceramic Capacitor [capacitance=100nF package="100 mil [THT, multilayer]"]
  22pf_2 = Ceramic Capacitor [capacitance=100nF package="100 mil [THT, multilayer]"]
  Q1 = Basic FET N-Channel [package="TO220 [THT]"]
  R3 = Resistor [tolerance=±5% resistance=220 package=THT]
  D1 = Rectifier Diode [part_number=1N4001 package="300 mil [THT]"]
  PWR = Battery block 9V
  8V_volt = Voltage Regulator - Variable [package="TO220 [THT]"]

nets:
  N1: Device_Output.Ring, Q1.drain, D1.anode
  N2: Device_Output.Tip, 5V_volt.input_voltage, D1.cathode
  N3: DC_12V_JACK.GND, Red_LED.cathode, R1.Pin_1
  N4: DC_12V_JACK.VCC, R2.Pin_1, 8V_volt.IN
  N5: Blue_LED.cathode, Green_LED.cathode, R1.Pin_0
  N6: Blue_LED.anode, ATMEGA_328P.D7
  N7: Green_LED.anode, ATMEGA_328P.D10_(PWM)
  N8: 5V_volt.GND, Buzzer.2, ATMEGA_328P.GND#21, 10UF.-, Q1.source, R3.Pin_1, PWR.-
  N9: 5V_volt.output_voltage, ATMEGA_328P.VCC, 10K.Pin_0, 10UF.+
  N10: Red_LED.anode, R2.Pin_0
  N11: Buzzer.1, ATMEGA_328P.D9_(PWM)
  N12: ATMEGA_328P.RESET, Reset.Pin_3, Reset.Pin_4
  N13: ATMEGA_328P.D3_(PWM), Q1.gate, R3.Pin_0
  N14: ATMEGA_328P.GND#7, 22pf.0, 22pf_2.0
  N15: ATMEGA_328P.XLAT1, 16MHz_C.pin_0, 22pf.1
  N16: ATMEGA_328P.XLAT2, 16MHz_C.pin_1, 22pf_2.1
  N17: 10K.Pin_1, Reset.Pin_2

notes:
  +
  in
  op
  Shreenandan
  BRAIN PBM V-2
  Design and  Developed in INDIA
  BRAIN PBM | Your Pocket Psychiatrist
  Blue LED
  Green LED
  Red LED
  8V Reg'r
  5V Reg'r
  BATTERY
  10uF
  12V DC Jack
  Buzzer
  10k OHM
  1k OHM
  MFET-N 540
  switch
  3.5 mm jack
  Bluetooth Port
  120BM0806 | 03-04-2024
